# Fritzing sketch final fritzing  (saved by Fritzing 0.9.3b)
breadboards: 1

parts:
  Nino_Panes_-_Succulent_Planter = Arduino Uno (Rev3)
  IC1 = H-Bridge [package=THT]
  M1 = DC Motor
  M2 = DC Motor

nets:
  N1: Nino_Panes_-_Succulent_Planter.D8, IC1.3_4EN
  GND: Nino_Panes_-_Succulent_Planter.GND, IC1.GND1, IC1.GND2, IC1.GND3, IC1.GND4
  N2: Nino_Panes_-_Succulent_Planter.D2, IC1.1_2EN
  N3: Nino_Panes_-_Succulent_Planter.D3_PWM, IC1.1A
  N4: Nino_Panes_-_Succulent_Planter.D4, IC1.2A
  N5: Nino_Panes_-_Succulent_Planter.D6_PWM, IC1.4A
  N6: Nino_Panes_-_Succulent_Planter.D7, IC1.3A
  N7: Nino_Panes_-_Succulent_Planter.5V, IC1.VCC2, IC1.VCC1
  N8: IC1.1Y, M2.pin_1
  N9: IC1.2Y, M2.pin_2
  N10: IC1.3Y, M1.pin_2
  N11: IC1.4Y, M1.pin_1
